# Fritzing sketch LCD version nGiegie (saved by Fritzing 0.9.0b)
circuit board: 6.88566cm x 5.36311cm
breadboards: 1

parts:
  UNO_R3 = Arduino Board Ethernet
  LCD_8x2 = LCD-16X2 [part_number=8x2 package=lcd-8x2-kit]
  R1 = Resistor [tolerance=±5% resistance=1k package=THT]
  R4 = Resistor [tolerance=±5% resistance=10k package=THT]
  R5 = Resistor [tolerance=±5% resistance=10k package=THT]
  R6 = Resistor [tolerance=±5% resistance=1k package=THT]
  Light_on/off = SPST Switch [package=switch-spdt_lock.007s]
  Sensor_connector = screw terminal, 5 pins
  R7 = Resistor [tolerance=±5% resistance=10k package=THT]
  R8 = Resistor [tolerance=±5% resistance=1k package=THT]
  J1 = Screw terminal - 5 pins [package=THT]

nets:
  N1: UNO_R3.D8, LCD_8x2.DB4
  GND: UNO_R3.GND, LCD_8x2.VSS, LCD_8x2.R_W, LCD_8x2.K, R6.Pin_0, Sensor_connector.pin1, J1.pin1
  N2: UNO_R3.A0, LCD_8x2.RS
  N3: UNO_R3.A1, LCD_8x2.E
  N4: UNO_R3.D2_PWM, R8.Pin_0
  N5: UNO_R3.D3_PWM, R1.Pin_0
  N6: UNO_R3.D5_PWM, LCD_8x2.DB5
  N7: UNO_R3.D6_PWM, LCD_8x2.DB6
  N8: UNO_R3.D7, LCD_8x2.DB7
  5V: UNO_R3.5V, LCD_8x2.VDD, R4.Pin_1, R5.Pin_1, Light_on/off.P, Sensor_connector.pin2, R7.Pin_1, J1.pin2
  N9: LCD_8x2.VO, R5.Pin_0, R6.Pin_1
  N10: LCD_8x2.A, Light_on/off.S
  N11: R1.Pin_1, R4.Pin_0, Sensor_connector.pin5, J1.pin5
  N12: Sensor_connector.pin3, J1.pin3
  N13: Sensor_connector.pin4, R7.Pin_0, R8.Pin_1, J1.pin4

notes:
  NGeigie LCD, Draft Safecast NGeigie_LCD, V0.8
  Safecast nGeigie_LCD Shield

custom parts:
  Screw terminal - 5 pins: Screw terminal with 5 pins
